# Fritzing sketch MultimetroBluetooth (saved by Fritzing 1.0.1rc)
breadboards: 1

parts:
  BT1 = Bluetooth HC-06u [package=THT]
  R1 = Resistor [tolerance=±5% resistance=220 package="0402 [SMD]"]
  R2 = Resistor [tolerance=±5% resistance=470 package="0402 [SMD]"]
  Componente1 = Arduino Uno (Rev3)
  S1 = Pushbutton [package="[THT]"]
  Mod1 = Voltage Sensor 25V

nets:
  VCC: BT1.VCC, Componente1.5V
  GND: BT1.GND, Componente1.GND, S1.Pin_3, S1.Pin_4, Mod1.GND, Mod1.-
  N1: BT1.TXD, Componente1.D2
  N2: BT1.RXD, R1.Pin_1
  N3: R1.Pin_0, R2.Pin_1
  N4: R2.Pin_0, Componente1.D3_PWM
  N5: Componente1.A0, Mod1.S
  N6: Componente1.D6_PWM, S1.Pin_1, S1.Pin_2

custom parts:
  Bluetooth HC-06u: Bluetooth HC-06 - face up, pins down 16.5mm x 37.5mm PCB
